# Fritzing sketch rukavica (saved by Fritzing 0.9.3b)
breadboards: 1

parts:
  Microcontroler = Arduino Nano (Rev3.0)
  R6 = Resistor [tolerance=±5% resistance=22k package=THT]
  J6 = Basic Force Sensing Resistor (FSR) [package=THT]
  R7 = Resistor [tolerance=±5% resistance=22k package=THT]
  J7 = Basic Force Sensing Resistor (FSR) [package=THT]
  R8 = Resistor [tolerance=±5% resistance=22k package=THT]
  J8 = Basic Force Sensing Resistor (FSR) [package=THT]
  R9 = Resistor [tolerance=±5% resistance=22k package=THT]
  J9 = Basic Force Sensing Resistor (FSR) [package=THT]
  R10 = Resistor [tolerance=±5% resistance=22k package=THT]
  J10 = Basic Force Sensing Resistor (FSR) [package=THT]

nets:
  N1: Microcontroler.A5, R9.Pin_1, J9.pin_0
  N2: Microcontroler.A4, R8.Pin_1, J8.pin_0
  N3: Microcontroler.A3, R7.Pin_1, J7.pin_0
  N4: Microcontroler.A2, R6.Pin_1, J6.pin_0
  5V: R6.Pin_0, R7.Pin_0, R8.Pin_0, R9.Pin_0, R10.Pin_0
  GND: J6.pin_1, J7.pin_1, J8.pin_1, J9.pin_1, J10.pin_1
  N5: R10.Pin_1, J10.pin_0
