# Fritzing sketch schematic-arm (saved by Fritzing 0.9.3b)
breadboards: 1

parts:
  Microcontroller = Arduino Nano (Rev3.0)
  Thumb = Basic Servo
  J2 = Basic Servo
  J3 = Basic Servo
  J4 = Basic Servo
  J5 = Basic Servo

nets:
  N1: Microcontroller.D9, J5.pulse
  N2: Microcontroller.D10, J4.pulse
  N3: Microcontroller.D11/MOSI, J3.pulse
  N4: Microcontroller.D12/MISO, J2.pulse
  N5: Microcontroller.D13/SCK, Thumb.pulse
  GND: Thumb.gnd, J2.gnd, J3.gnd, J4.gnd, J5.gnd
  5V: Thumb.vcc, J2.vcc, J3.vcc, J4.vcc, J5.vcc
