# Fritzing sketch schematic-glove (saved by Fritzing 0.9.3b)
breadboards: 1

parts:
  Част1 = Arduino Nano (Rev3.0)
  R1 = Resistor [tolerance=±5% resistance=22k package=THT]
  J1 = Basic Force Sensing Resistor (FSR) [package=THT]
  R2 = Resistor [tolerance=±5% resistance=22k package=THT]
  J2 = Basic Force Sensing Resistor (FSR) [package=THT]
  R3 = Resistor [tolerance=±5% resistance=22k package=THT]
  J3 = Basic Force Sensing Resistor (FSR) [package=THT]
  R4 = Resistor [tolerance=±5% resistance=22k package=THT]
  J4 = Basic Force Sensing Resistor (FSR) [package=THT]
  R5 = Resistor [tolerance=±5% resistance=22k package=THT]
  J5 = Basic Force Sensing Resistor (FSR) [package=THT]

nets:
  GND: Част1.GND, J1.pin_1, J2.pin_1, J3.pin_1, J4.pin_1, J5.pin_1
  N1: Част1.A5, R5.Pin_1, J5.pin_0
  N2: Част1.A4, R4.Pin_1, J4.pin_0
  N3: Част1.A3, R3.Pin_1, J3.pin_0
  N4: Част1.A2, R2.Pin_1, J2.pin_0
  N5: Част1.A0, R1.Pin_1, J1.pin_0
  5V: R1.Pin_0, R2.Pin_0, R3.Pin_0, R4.Pin_0, R5.Pin_0
